// Digital circuit main.dig as structural Verilog
module main (
  input  clk,
  input  reset,
  output [23:0] b,
  output [31:0] a,
  output [31:0] f,
  output [23:0] e,
  output [23:0] i,
  output [7:0] h,
  output [7:0] d,
  output [7:0] g,
  output [7:0] c,
  output [7:0] k,
  output [31:0] j,
  output [31:0] l,
  output [31:0] m,
  output [31:0] p,
  output [15:0] term_data,
  output [15:0] vram_addr,
  output term_we,
  output [31:0] r,
  output [31:0] n,
  output a1,
  output [7:0] a2,
  output [7:0] a3,
  output [23:0] t8
);

  wire alu_cout, alu_nout, alu_nzout, alu_vout, alu_zout, and_3_out, and_4_out, comparator_1_eq,
       comparator_2_eq, cond, ctrl_addr_csel, ctrl_branch_en, ctrl_cin_sel, ctrl_flags_we, ctrl_jump_type,
       ctrl_mem_rd, ctrl_mem_wr, flag_c, flag_n, flag_v, flag_z, HALT_IN, is_mmio, mem_rd_out, pc_branch_en,
       pc_jump_uncond, pc_mux_sel_1, pc_mux_sel_2, ram_cs, seq_exec, seq_fetch, sp_load_n, vram_we;
  wire [1:0] ctrl_cycles, ctrl_shift_op, ctrl_sp_op;
  wire [2:0] b_main_sel, ctrl_bus_sel, ctrl_wb_sel;
  wire [4:0] ctrl_alu_pre;
  wire [15:0] vram_data;
  wire [23:0] CPU_ADDR_OUT, mem_addr, mem_addr_in, mmio_addr, sp_delta;
  wire [31:0] alu_b, io_data_in, mem_eeprom_out, reg_c, shift_out;

  and and_1 (pc_branch_en, ctrl_branch_en, seq_exec);
  and and_2 (pc_jump_uncond, ctrl_jump_type, seq_exec);
  sequencer sequencer_1 (
    .reset(reset), .cycles(ctrl_cycles), .CLK(clk), .FETCH(seq_fetch), .EXECUTE(seq_exec));  // open: MEM_WAIT
  // pc pc_1: pin names not known; wires that end beside it: clk, reset, i, e, t8, pc_mux_sel_1, pc_mux_sel_2, flag_n, flag_c, flag_z, flag_v, cond, pc_branch_en, 1'b0, HALT_IN, 1'b0, 1'b1, 1'b1, 1'b1, sp_delta, sp_load_n, pc_jump_uncond, seq_fetch, b, t8
  mmio_bus mmio_bus_1 (.ADDR(mem_addr), .CPU_ADDR_OUT(CPU_ADDR_OUT), .mmio_addr(mmio_addr), .is_mmio(is_mmio));
  register register_1 (
    .WE(a1), .DATA_W(m), .ADDR_A(a2), .ADDR_B(d), .ADDR_W(a3), .EXEC(seq_exec), .addr_c_sel(ctrl_addr_csel),
    .ir_bus(f), .clk(clk), .DATA_A(n), .DATA_B(r), .DATA_C(reg_c));
  // ir ir_1: pin names not known; wires that end beside it: a, seq_fetch, clk, f, c, a2, d, a3, i, e, cond
  bus_arbitration bus_arbitration_1 (
    .FETCH(seq_fetch), .PC_OUT(b), .IR_ADDR(i), .Reg_A(j), .MEM_RD_IN(ctrl_mem_rd), .addr_sel(ctrl_bus_sel),
    .Reg_b(32'h1), .Reg_A_off(32'h1), .Reg_B_off(32'h1), .Reg_AB(32'h1), .PC_offset(32'h1), .SP_out(32'h1),
    .Alu_in(32'h1), .ADDR_BUS(mem_addr), .MEM_RD_OUT(mem_rd_out));
  io_controller io_controller_1 (
    .mem_addr(mmio_addr), .c_wr(ctrl_mem_wr), .kb_data(16'h1), .mem_data_out(r), .io_data_in(io_data_in),
    .ram_cs(ram_cs), .vram_we(vram_we), .vram_addr(vram_addr), .vram_data(vram_data), .term_we(term_we),
    .term_data(term_data));
  EEPROMDualPort #(.AddrBits(24), .Bits(32)) eepromdualport_1 (
    .A(mem_addr), .Din(r), .str(ctrl_mem_wr), .C(clk), .ld(mem_rd_out), .D(mem_eeprom_out));
  Multiplexer #(.Bits(32)) multiplexer_1 (.sel(ram_cs), .in_0(mem_eeprom_out), .in_1(io_data_in), .out(a));
  microcode microcode_1 (
    .op(c), .alu_op(k), .alu_pre(ctrl_alu_pre), .cin_sel(ctrl_cin_sel), .wb_sel(ctrl_wb_sel),
    .shift_op(ctrl_shift_op), .flags_we(ctrl_flags_we), .reg_we(a1), .mem_rd(ctrl_mem_rd),
    .mem_wr(ctrl_mem_wr), .addr_csel(ctrl_addr_csel), .branch_en(ctrl_branch_en), .jump_type(ctrl_jump_type),
    .sp_op(ctrl_sp_op), .cycles(ctrl_cycles), .ctrl_bus_sel(ctrl_bus_sel), .b_main_sel(b_main_sel),
    .pc_rel(pc_mux_sel_1));  // open: unused
  Comparator #(.Bits(8)) comparator_1 (.a(8'h2), .b(a3), .eq(comparator_1_eq));  // open: gt, lt
  b_mux b_mux_1 (.ir(f), .reg_b(r), .sel(b_main_sel), .alu_b(alu_b));
  and and_3 (and_3_out, seq_exec, a1, comparator_1_eq);
  // shift shift_1: pin names not known; wires that end beside it: n, ctrl_shift_op, r, shift_out
  alu_32b_final alu_32b_final_1 (
    .A(n), .nz0(1'b0), .B(alu_b), .Opcode(k), .control(ctrl_alu_pre), .REG_C(reg_c), .cin_sel(ctrl_cin_sel),
    .FLAG_C(flag_c), .vout(alu_vout), .zout(alu_zout), .nzout(alu_nzout), .nout(alu_nout), .Out(j),
    .cout(alu_cout));
  flag_reg flag_reg_1 (
    .ZERO_IN(alu_zout), .CARRY_IN(alu_cout), .NEGATIVE_IN(alu_nout), .OVERFLOW_IN(alu_vout),
    .FLAG_WE(ctrl_flags_we), .CLK(clk), .EXEC(seq_exec), .FLAG_Z(flag_z), .FLAG_C(flag_c), .FLAG_N(flag_n),
    .FLAG_O(flag_v));
  wb_mux wb_mux_1 (
    .wb_sel(ctrl_wb_sel), .alu_out(j), .shift_out(shift_out), .pc_save(t8), .mem_din(a),
    .io_datain(io_data_in), .reg_a(n), .ir_bus(f), .reg_w_data(m));
  Register #(.Bits(32)) register_2 (.D(alu_b), .C(clk), .en(and_3_out), .Q(p));
  Multiplexer #(.Bits(24)) multiplexer_2 (.sel(and_4_out), .in_0(CPU_ADDR_OUT), .in_1(mmio_addr), .out(mem_addr_in));
  and and_4 (and_4_out, is_mmio, mem_rd_out);
  and and_5 (HALT_IN, comparator_2_eq, seq_exec);
  Comparator #(.Bits(8)) comparator_2 (.a({8{1'b1}}), .b(c), .eq(comparator_2_eq));  // open: gt, lt
  Comparator #(.Bits(8)) comparator_3 (.a(f[31:24]), .b(8'h33), .eq(pc_mux_sel_2));  // open: gt, lt
  Multiplexer #(.Selector_Bits(2), .Bits(24)) multiplexer_3 (
    .sel(ctrl_sp_op), .in_0({24{1'b0}}), .in_1(24'h1), .in_2({24{1'b1}}), .in_3({24{1'b0}}), .out(sp_delta));
  nor nor_1 (sp_load_n, ctrl_sp_op[0], ctrl_sp_op[1]);

  assign g = a2;
  assign h = a3;
  assign l = a;

  // Other names for the same wires on the sheet: alu_out[31:0] = j; ctrl_alu_op[7:0] = k; ctrl_reg_we = a1;
  //   IR_ADDR[23:0] = i; ir_addr_a[7:0] = a2; ir_addr_b[7:0] = d; ir_addr_w[7:0] = a3; ir_bus[31:0] = f;
  //   ir_24_31[7:0] = f[31:24]; ir_offset[23:0] = e; ir_opcode[7:0] = c; mem_din[31:0] = a; pc_out[23:0] = b;
  //   pc_save[23:0] = t8; reg_a[31:0] = n; reg_b[31:0] = r; reg_w_data[31:0] = m

  // Notes on the sheet:
  //   clk: Hz: 80
  //   reset: default 1
  //   contents of eepromdualport_1 (hex, n*v repeats v):
  //   22000a01,22000a02,22000003,22000000,1010203,1000302,30000004
endmodule
